// Digital circuit reg_file.dig as structural Verilog
module reg_file (
  input  [2:0] RS1,
  input  [2:0] RS2,
  input  [2:0] WS,
  input  WE,
  input  [15:0] IN,
  input  clk,
  input  [3:0] FLIN,
  input  FLEN,
  input  IN_high,
  output [15:0] OUT1,
  output [15:0] OUT2,
  output [3:0] FOUT,
  output [15:0] PC
);

  wire and_1_out, demultiplexer_2_out_1, demultiplexer_2_out_2, demultiplexer_2_out_3, demultiplexer_2_out_4,
       demultiplexer_2_out_5, demultiplexer_2_out_6, demultiplexer_2_out_7;
  wire [15:0] and_2_out, demultiplexer_1_out_0, demultiplexer_1_out_1, demultiplexer_1_out_2,
       demultiplexer_1_out_3, demultiplexer_1_out_4, demultiplexer_1_out_6, demultiplexer_1_out_7,
       multiplexer_1_out, multiplexer_2_out, multiplexer_3_out, or_1_out, plus_1_s, R1_q, R2_q, R3_q, R4_q,
       R6_q, ZR_q;
  wire [15:4] FL_q;

  Multiplexer #(.Bits(16)) multiplexer_1 (.sel(IN_high), .in_0(IN), .in_1(or_1_out), .out(multiplexer_1_out));
  Demultiplexer #(.Selector_Bits(3), .Bits(16)) demultiplexer_1 (
    .sel(WS), .in(multiplexer_1_out), .out_0(demultiplexer_1_out_0), .out_1(demultiplexer_1_out_1),
    .out_2(demultiplexer_1_out_2), .out_3(demultiplexer_1_out_3), .out_4(demultiplexer_1_out_4),
    .out_6(demultiplexer_1_out_6), .out_7(demultiplexer_1_out_7));  // open: out_5
  Multiplexer #(.Bits(16)) multiplexer_2 (
    .sel(demultiplexer_2_out_7), .in_0(plus_1_s), .in_1(demultiplexer_1_out_7), .out(multiplexer_2_out));
  Demultiplexer #(.Selector_Bits(3)) demultiplexer_2 (
    .sel(WS), .in(WE), .out_1(demultiplexer_2_out_1), .out_2(demultiplexer_2_out_2),
    .out_3(demultiplexer_2_out_3), .out_4(demultiplexer_2_out_4), .out_5(demultiplexer_2_out_5),
    .out_6(demultiplexer_2_out_6), .out_7(demultiplexer_2_out_7));  // open: out_0
  and and_1 (and_1_out, FLEN, demultiplexer_2_out_5);
  Register #(.Bits(16)) ZR (.D(demultiplexer_1_out_0), .C(clk), .en(1'b0), .Q(ZR_q));
  Register #(.Bits(16)) R1 (.D(demultiplexer_1_out_1), .C(clk), .en(demultiplexer_2_out_1), .Q(R1_q));
  Register #(.Bits(16)) R2 (.D(demultiplexer_1_out_2), .C(clk), .en(demultiplexer_2_out_2), .Q(R2_q));
  Register #(.Bits(16)) R3 (.D(demultiplexer_1_out_3), .C(clk), .en(demultiplexer_2_out_3), .Q(R3_q));
  Register #(.Bits(16)) R4 (.D(demultiplexer_1_out_4), .C(clk), .en(demultiplexer_2_out_4), .Q(R4_q));
  Register #(.Bits(16)) FL (.D({{12{1'b0}}, FLIN}), .C(clk), .en(and_1_out), .Q({FL_q, FOUT}));
  Register #(.Bits(16)) R6 (.D(demultiplexer_1_out_6), .C(clk), .en(demultiplexer_2_out_6), .Q(R6_q));
  Register #(.Bits(16)) u_PC (.D(multiplexer_2_out), .C(clk), .en(1'b1), .Q(PC));
  Add #(.Bits(16)) plus_1 (.a(16'h1), .b(PC), .c_i(1'b0), .s(plus_1_s));  // open: c_o
  assign or_1_out = {IN[7:0], {8{1'b0}}} | and_2_out;  // Or or_1, 16 bits wide
  assign and_2_out = 16'hff & multiplexer_3_out;  // And and_2, 16 bits wide
  Multiplexer #(.Selector_Bits(3), .Bits(16)) multiplexer_3 (
    .sel(WS), .in_0(ZR_q), .in_1(R1_q), .in_2(R2_q), .in_3(R3_q), .in_4(R4_q), .in_5({FL_q, FOUT}),
    .in_6(R6_q), .in_7(PC), .out(multiplexer_3_out));
  Multiplexer #(.Selector_Bits(3), .Bits(16)) multiplexer_4 (
    .sel(RS1), .in_0(ZR_q), .in_1(R1_q), .in_2(R2_q), .in_3(R3_q), .in_4(R4_q), .in_5({FL_q, FOUT}),
    .in_6(R6_q), .in_7(PC), .out(OUT1));
  Multiplexer #(.Selector_Bits(3), .Bits(16)) multiplexer_5 (
    .sel(RS2), .in_0(ZR_q), .in_1(R1_q), .in_2(R2_q), .in_3(R3_q), .in_4(R4_q), .in_5({FL_q, FOUT}),
    .in_6(R6_q), .in_7(PC), .out(OUT2));

  // Notes on the sheet:
  //   RS1: The index of the register which should output its value to OUT1.
  //   RS2: The index of the register which should output its value to OUT2.
  //   WS: The index of the register which should save the value on IN on the next clock cycle (if WE is high).
  //   WE: Whether the register selected by WS should save the value from IN on the next cycle.
  //   IN: The value to be saved into the register specified by WS if WE is high,
  //   OUT1: The value in the register specified by RS1.
  //   OUT2: The value in the register specified by RS2.
  //   FLIN: The index of the register which should save the value on IN on the next clock cycle (if WE is high).
  //   FLEN: The index of the register which should save the value on IN on the next clock cycle (if WE is high).
  //   FOUT: The value in the register specified by RS2.
  //   PC: The value in the register specified by RS1.
  //   IN_high: The index of the register which should save the value on IN on the next clock cycle (if WE is high).
endmodule

/* Test case:
clk RS1 RS2 WS WE IN OUT1 OUT2
c 0 0 0 1 0x1234 0x0000 0x0000
c 1 0 1 1 0xBEEF 0xBEEF 0x0000
c 2 1 2 1 0xDEAD 0xDEAD 0xBEEF
c 3 2 3 1 0xFFFF 0xFFFF 0xDEAD
c 3 2 3 0 0xABCD 0xFFFF 0xDEAD
c 3 2 2 0 0xABCD 0xFFFF 0xDEAD
c 1 0 1 0 0xABCD 0xBEEF 0x0000
c 1 0 0 0 0xABCD 0xBEEF 0x0000
c 1 0 2 1 0xBADE 0xBEEF 0x0000
c 0 2 2 1 0xBADE 0x0000 0xBADE
c 0 0 2 0 0x1234 0x0000 0x0000
c 2 3 0 1 0x0000 0xBADE 0xFFFF
c 0 0 2 0 0x1234 0x0000 0x0000
*/
